# Fritzing sketch receiver_schematic (saved by Fritzing 0.8.7b)
breadboards: 1

parts:
  2N5089 = NPN-Transistor [package="TO92 [THT]"]
  R1 = Resistor [tolerance=±5% resistance=220 package=THT]
  R2 = Resistor [tolerance=±5% resistance=220 package=THT]
  R3 = Resistor [tolerance=±5% resistance=220 package=THT]
  R4 = Resistor [tolerance=±5% resistance=220 package=THT]
  C1 = Ceramic Capacitor [capacitance=100nF package="100 mil [THT, multilayer]"]
  C2 = Ceramic Capacitor [capacitance=100nF package="100 mil [THT, multilayer]"]
  SPKR1 = Loudspeaker
  R5 = Resistor [tolerance=±5% resistance=220 package=THT]
  C3 = Ceramic Capacitor [capacitance=100nF package="100 mil [THT, multilayer]"]
  D1 = Rectifier Diode [part_number=1N4001 package="300 mil [THT]"]
  R6 = Resistor [tolerance=±5% resistance=220 package=THT]
  R7 = Resistor [tolerance=±5% resistance=220 package=THT]
  C4 = Ceramic Capacitor [capacitance=100nF package="100 mil [THT, multilayer]"]
  C5 = Ceramic Capacitor [capacitance=100nF package="100 mil [THT, multilayer]"]
  L1 = Inductor [package="400 mil [THT]"]
  R8 = Resistor [tolerance=±5% resistance=220 package=THT]
  ANT1 = Antenna

nets:
  N1: 2N5089.E, R2.Pin_1
  N2: 2N5089.B, R3.Pin_0, R4.Pin_1, C1.0
  N3: 2N5089.C, R1.Pin_0, C2.1
  5V: R1.Pin_1, R3.Pin_1, R6.Pin_1
  GND: R2.Pin_0, R4.Pin_0, SPKR1.pin2, C3.0, R7.Pin_0, C5.0, L1.pin_1
  N4: C1.1, R5.Pin_1, C3.1
  N5: C2.0, SPKR1.pin1
  N6: R5.Pin_0, D1.cathode
  N7: D1.anode, R6.Pin_0, R7.Pin_1, C4.0
  N8: C4.1, C5.1, L1.pin_0, R8.Pin_1
  N9: R8.Pin_0, ANT1.antenna_lead
